// Logisim project regfile.circ as structural Verilog: 3 circuits, main circuit main
module main (
  input  [4:0] Read_Register_1_rs1,
  input  [4:0] Read_Register_2_rs2,
  input  [4:0] Write_Register_rd,
  input  [31:0] Write_Data,
  input  Write_Enable,
  input  Clock,
  output [31:0] ra,
  output [31:0] sp,
  output [31:0] t0,
  output [31:0] t1,
  output [31:0] t2,
  output [31:0] s0,
  output [31:0] s1,
  output [31:0] a0,
  output [31:0] Read_Data_1,
  output [31:0] Read_Data_2
);

  regfile regfile_1 (
    .write_register(Write_Register_rd), .write_enable(Write_Enable), .clk(Clock), .wln(Write_Data),
    .read_register_2(Read_Register_2_rs2), .read_register_1(Read_Register_1_rs1), .read_data1(Read_Data_1),
    .read_data2(Read_Data_2), .ra(ra), .sp(sp), .t0(t0), .t1(t1), .t2(t2), .s0(s0), .s1(s1), .a0(a0));

  // Other names for the same wires on the sheet: clk = Clock; read_data1[31:0] = Read_Data_1;
  //   read_data2[31:0] = Read_Data_2; read_reg1[4:0] = Read_Register_1_rs1; read_reg2[4:0] = Read_Register_2_rs2;
  //   write_en = Write_Enable; write_reg[4:0] = Write_Register_rd

  // Notes on the sheet:
  //   INPUTS to your circuit
  //   DON'T CHANGE THE LOCATIONS OF THE INPUTS AND OUTPUTS!
  //   These are DEBUG/TEST outputs from your circuit.
  //   OUTPUTS from your circuit
endmodule

module regfile (
  input  [4:0] write_register,
  input  write_enable,
  input  clk,
  input  [31:0] wln,
  input  [4:0] read_register_2,
  input  [4:0] read_register_1,
  output [31:0] read_data1,
  output [31:0] read_data2,
  output [31:0] ra,
  output [31:0] sp,
  output [31:0] t0,
  output [31:0] t1,
  output [31:0] t2,
  output [31:0] s0,
  output [31:0] s1,
  output [31:0] a0
);

  wire demultiplexer_1_out1, demultiplexer_1_out2, demultiplexer_1_out5, demultiplexer_1_out6,
       demultiplexer_1_out7, demultiplexer_1_out8, demultiplexer_1_out9, demultiplexer_1_out10;

  Multiplexer #(.select(5), .width(32), .enable("false")) multiplexer_1 (
    .in0({32{1'b0}}), .in1(ra), .in2(sp), .in5(t0), .in6(t1), .in7(t2), .in8(s0), .in9(s1), .in10(a0),
    .out(read_data1), .sel(read_register_1));  // open: in3, in4, in11, in12, in13, in14, in15, in16, in17, in18, in19, in20, in21, in22, in23, in24, in25, in26, in27, in28, in29, in30, in31
  register_gated x1 (.Output_(ra), .clk(clk), .wenable(demultiplexer_1_out1), .input_(wln));
  register_gated x2 (.Output_(sp), .clk(clk), .wenable(demultiplexer_1_out2), .input_(wln));
  register_gated x5 (.Output_(t0), .clk(clk), .wenable(demultiplexer_1_out5), .input_(wln));
  register_gated x6 (.Output_(t1), .clk(clk), .wenable(demultiplexer_1_out6), .input_(wln));
  register_gated x7 (.Output_(t2), .clk(clk), .wenable(demultiplexer_1_out7), .input_(wln));
  Demultiplexer #(.select(5)) demultiplexer_1 (
    .out1(demultiplexer_1_out1), .out2(demultiplexer_1_out2), .out5(demultiplexer_1_out5),
    .out6(demultiplexer_1_out6), .out7(demultiplexer_1_out7), .out8(demultiplexer_1_out8),
    .out9(demultiplexer_1_out9), .out10(demultiplexer_1_out10), .in(1'b1), .sel(write_register),
    .en(write_enable));  // open: out0, out3, out4, out11, out12, out13, out14, out15, out16, out17, out18, out19, out20, out21, out22, out23, out24, out25, out26, out27, out28, out29, out30, out31
  register_gated x8 (.Output_(s0), .clk(clk), .wenable(demultiplexer_1_out8), .input_(wln));
  register_gated x9 (.Output_(s1), .clk(clk), .wenable(demultiplexer_1_out9), .input_(wln));
  register_gated x10 (.Output_(a0), .clk(clk), .wenable(demultiplexer_1_out10), .input_(wln));
  Multiplexer #(.select(5), .width(32), .enable("false")) multiplexer_2 (
    .in0({32{1'b0}}), .in1(ra), .in2(sp), .in5(t0), .in6(t1), .in7(t2), .in8(s0), .in9(s1), .in10(a0),
    .out(read_data2), .sel(read_register_2));  // open: in3, in4, in11, in12, in13, in14, in15, in16, in17, in18, in19, in20, in21, in22, in23, in24, in25, in26, in27, in28, in29, in30, in31

  // Other names for the same wires on the sheet: x1_output[31:0] = ra; x2_output[31:0] = sp; x5_output[31:0] = t0;
  //   x6_output[31:0] = t1; x7_output[31:0] = t2; x8_output[31:0] = s0; x9_output[31:0] = s1; x10_output[31:0] = a0
endmodule

module register_gated (
  input  [31:0] input_,
  input  wenable,
  input  clk,
  output [31:0] Output_
);

  Register #(.width(32)) register_1 (.D(input_), .en(wenable), .clk(clk), .Q(Output_));  // open: clr
endmodule
