// Logisim project alu.circ as structural Verilog: 1 circuit, main circuit alu
module alu (
  input  [31:0] A,
  input  [31:0] B,
  input  [3:0] ALUSel,
  output [31:0] Result
);

  wire [0:0] slt_a8681656;
  wire [31:0] add, and_37c6bfe4, div_776f8997, mul_, mulh_a224778b, or_d3720a59, rem_2c570c2a, sll_35c5fbb0,
       sra_2457ac41, srl_9926c470, sub_045e7214, xor_db3e3cd8;

  Adder #(.width(32)) adder_1 (.a(A), .b(B), .out(add));  // open: cin, cout
  assign and_37c6bfe4 = A & B;  // AND_Gate and_1, 32 bits wide
  assign or_d3720a59 = A | B;  // OR_Gate or_1, 32 bits wide
  Multiplier #(.width(32)) multiplier_1 (.a(A), .b(B), .out(mul_));  // open: cin, cout
  Subtractor #(.width(32)) subtractor_1 (.a(A), .b(B), .out(sub_045e7214));  // open: bin, bout
  assign xor_db3e3cd8 = A ^ B;  // XOR_Gate xor_1, 32 bits wide
  Multiplier #(.width(32)) multiplier_2 (.a(A), .b(B), .cout(mulh_a224778b));  // open: out, cin
  Multiplexer #(.select(4), .width(32), .enable("false")) multiplexer_1 (
    .in0(add), .in1(mul_), .in2(sub_045e7214), .in3(sll_35c5fbb0), .in4(mulh_a224778b),
    .in5({{31{1'b0}}, slt_a8681656[0]}), .in6(xor_db3e3cd8), .in7(div_776f8997), .in8(srl_9926c470),
    .in9(or_d3720a59), .in10(rem_2c570c2a), .in11(and_37c6bfe4), .in12(sra_2457ac41), .in13(B), .out(Result),
    .sel(ALUSel));  // open: in14, in15
  Shifter #(.width(32), .shift("lr")) shifter_1 (.in(A), .\dist (B[4:0]), .out(srl_9926c470));
  Shifter #(.width(32), .shift("ar")) shifter_2 (.in(A), .\dist (B[4:0]), .out(sra_2457ac41));
  Divider #(.width(32)) divider_1 (.a(A), .b(B), .out(div_776f8997), .rem(rem_2c570c2a));  // open: upper
  Shifter #(.width(32)) shifter_3 (.in(A), .\dist (B[4:0]), .out(sll_35c5fbb0));
  Comparator #(.width(32)) comparator_1 (.a(A), .b(B), .lt(slt_a8681656[0]));  // open: gt, eq

  // Other names for the same wires on the sheet: bsel_0aadbc23[31:0] = B

  // Notes on the sheet:
  //   INPUTS to your circuit
  //   DON'T CHANGE THE LOCATIONS OF THE INPUTS AND OUTPUTS!
  //   OUTPUT from your circuit
endmodule
