// Logisim project cpu.circ as structural Verilog: 8 circuits, main circuit main
module main (
  input  [31:0] INSTRUCTION,
  input  CLOCK,
  output [31:0] FETCH_ADDRESS,
  output [31:0] ra,
  output [31:0] sp,
  output [31:0] t0,
  output [31:0] t1,
  output [31:0] t2,
  output [31:0] s0,
  output [31:0] s1,
  output [31:0] a0
);

  wire Branch_breq, Branch_brlt, control_logic_1_asel, control_logic_1_brun, control_logic_1_bsel,
       control_logic_1_memrw, control_logic_1_pcsel, control_logic_1_regwen;
  wire [1:0] control_logic_1_wbsel;
  wire [2:0] control_logic_1_immsel, control_logic_1_load_sel, control_logic_1_output_type_sel;
  wire [3:0] control_logic_1_alusel;
  wire [31:0] adder_1_out, ALU_cefb238f_result, if_ex_control_1_alu_out_6acabea4,
       if_ex_control_1_instruction_out_f61fd319, if_ex_control_1_pc_out_758b2ec9,
       if_ex_control_1_pc_puls_4_out, IMM_Gen__output_c6659906, jalr_type_lshift_1_output_99ad1175,
       jalr_type_rshift_1_output_a7d0038a, load_control_1_output_05da9558, main_1_read_data_1,
       main_1_read_data_2, MEM_p5, multiplexer_1_out, multiplexer_2_out, multiplexer_3_out,
       multiplexer_4_out, shifter_1_out;

  Multiplexer #(.width(32), .enable("false")) multiplexer_1 (
    .in0(adder_1_out), .in1(if_ex_control_1_alu_out_6acabea4), .out(multiplexer_1_out),
    .sel(control_logic_1_pcsel));
  Register #(.width(32)) PC (.D(multiplexer_1_out), .clk(CLOCK), .Q(FETCH_ADDRESS));  // open: en, clr
  Adder #(.width(32)) adder_1 (.a(FETCH_ADDRESS), .b(32'h1), .out(adder_1_out));  // open: cin, cout
  Shifter #(.width(32)) shifter_1 (.in(adder_1_out), .\dist (5'b00010), .out(shifter_1_out));
  jalr_type_Lshift jalr_type_lshift_1 (
    .output_99ad1175(jalr_type_lshift_1_output_99ad1175), .type_sel(control_logic_1_output_type_sel),
    .input_0c2948f0(FETCH_ADDRESS));
  IF_EX_control if_ex_control_1 (
    .ALU_OUT_6acabea4(if_ex_control_1_alu_out_6acabea4), .PC_OUT_758b2ec9(if_ex_control_1_pc_out_758b2ec9),
    .PC_PULS_4_OUT(if_ex_control_1_pc_puls_4_out), .instruction(INSTRUCTION),
    .PC_6faf80e7(jalr_type_lshift_1_output_99ad1175), .ALU_6e8fb84a(ALU_cefb238f_result),
    .PC_PLUS_4(shifter_1_out), .instruction_OUT_f61fd319(if_ex_control_1_instruction_out_f61fd319),
    .clock(CLOCK), .branch_eq(CLOCK));  // open: branch_lt
  IMM_Gen IMM_Gen_ (
    .instruction(if_ex_control_1_instruction_out_f61fd319), .Output_c6659906(IMM_Gen__output_c6659906),
    .ImmSel(control_logic_1_immsel));
  Control_Logic control_logic_1 (
    .PCSel(control_logic_1_pcsel), .instruction(if_ex_control_1_instruction_out_f61fd319),
    .MemRW(control_logic_1_memrw), .BrLT(Branch_brlt), .BrEq(Branch_breq), .ASel(control_logic_1_asel),
    .BSel(control_logic_1_bsel), .RegWEn(control_logic_1_regwen), .BrUn(control_logic_1_brun),
    .ALUSel(control_logic_1_alusel), .WBSel(control_logic_1_wbsel), .ImmSel(control_logic_1_immsel),
    .load_Sel(control_logic_1_load_sel), .output_type_Sel(control_logic_1_output_type_sel));
  regfile_main main_1 (
    .Read_Register_1_rs1(if_ex_control_1_instruction_out_f61fd319[19:15]),
    .Read_Register_2_rs2(if_ex_control_1_instruction_out_f61fd319[24:20]),
    .Write_Register_rd(if_ex_control_1_instruction_out_f61fd319[11:7]), .Write_Data(multiplexer_4_out),
    .Write_Enable(control_logic_1_regwen), .Clock(CLOCK), .Read_Data_1(main_1_read_data_1),
    .Read_Data_2(main_1_read_data_2), .ra(ra), .sp(sp), .t0(t0), .t1(t1), .t2(t2), .s0(s0), .s1(s1), .a0(a0));
  branch_Comp Branch (
    .BrEq(Branch_breq), .B(main_1_read_data_2), .BrUn(control_logic_1_brun), .BrLT(Branch_brlt),
    .A(main_1_read_data_1));
  jalr_type_Rshift jalr_type_rshift_1 (
    .immSel_50e67bb1(control_logic_1_output_type_sel), .output_a7d0038a(jalr_type_rshift_1_output_a7d0038a),
    .intput_6fd505b9(main_1_read_data_1));
  Multiplexer #(.width(32), .enable("false")) multiplexer_2 (
    .in0(jalr_type_rshift_1_output_a7d0038a), .in1(if_ex_control_1_pc_out_758b2ec9), .out(multiplexer_2_out),
    .sel(control_logic_1_asel));
  Multiplexer #(.width(32), .enable("false")) multiplexer_3 (
    .in0(main_1_read_data_2), .in1(IMM_Gen__output_c6659906), .out(multiplexer_3_out),
    .sel(control_logic_1_bsel));
  alu ALU_cefb238f (
    .Result(ALU_cefb238f_result), .ALUSel(control_logic_1_alusel), .B(multiplexer_3_out),
    .A(multiplexer_2_out));
  // mem_main MEM: pin names not known; wires that end beside it: ALU_cefb238f_result, main_1_read_data_2, control_logic_1_memrw, CLOCK, MEM_p5
  load_control load_control_1 (
    .output_05da9558(load_control_1_output_05da9558), .load_Sel(control_logic_1_load_sel), .MEMData(MEM_p5));
  Multiplexer #(.select(2), .width(32), .enable("false")) multiplexer_4 (
    .in0(load_control_1_output_05da9558), .in1(ALU_cefb238f_result), .in2(if_ex_control_1_pc_puls_4_out),
    .out(multiplexer_4_out), .sel(control_logic_1_wbsel));  // open: in3

  // Other names for the same wires on the sheet: a0_441f0deb[31:0] = a0; clk = CLOCK;
  //   fetch_addr[31:0] = FETCH_ADDRESS; ra_d292739a[31:0] = ra; s0_b85451fb[31:0] = s0; s1_64c63a77[31:0] = s1;
  //   sp_ae7584c9[31:0] = sp; t0_8142ff9c[31:0] = t0; t1_a6a446c9[31:0] = t1; t2_23002d13[31:0] = t2

  // Notes on the sheet:
  //   Output
  //   pc+4
  //   alu
  //   pc+4
  //   alu
  //   PCSel
  //   Inputs/Outputs from run.circ. DO NOT MOVE THESE.
  //   Inputs
  //   pc+4
  //   jalr_type_shift
  //   Imm[31:0]
  //   writeData(wb)
  //   pc+4
  //   alu
  //   PC
  //   reg[rs1]
  //   Inputs/Outputs from run.circ. DO NOT MOVE THESE.
  //   PC
  //   Reg[rs2]
  //   ASel
  //   Bsel
  //   reg[rs2]
  //   MemRW
  //   WBSel
endmodule

module IMM_Gen (
  input  [31:0] instruction,
  input  [2:0] ImmSel,
  output [31:0] Output_c6659906
);

  wire [31:0] bit_extender_1_out, bit_extender_2_out, bit_extender_3_out, bit_extender_4_out,
       demultiplexer_1_out1, demultiplexer_1_out2, demultiplexer_1_out3, demultiplexer_1_out4,
       demultiplexer_1_out5, shifter_1_out, shifter_2_out;

  Demultiplexer #(.select(3), .width(32), .enable("false")) demultiplexer_1 (
    .out1(demultiplexer_1_out1), .out2(demultiplexer_1_out2), .out3(demultiplexer_1_out3),
    .out4(demultiplexer_1_out4), .out5(demultiplexer_1_out5), .in(instruction), .sel(ImmSel));  // open: out0, out6, out7
  assign bit_extender_1_out = {{20{demultiplexer_1_out1[31]}}, demultiplexer_1_out1[31:20]};  // Bit_Extender bit_extender_1
  assign bit_extender_2_out = {{20{demultiplexer_1_out2[31]}}, {demultiplexer_1_out2[31:25], demultiplexer_1_out2[11:7]}};  // Bit_Extender bit_extender_2
  assign bit_extender_3_out = {{19{demultiplexer_1_out3[31]}}, {demultiplexer_1_out3[31], demultiplexer_1_out3[7], demultiplexer_1_out3[30:25], demultiplexer_1_out3[11:8], 1'b0}};  // Bit_Extender bit_extender_3
  assign bit_extender_4_out = {{11{demultiplexer_1_out5[31]}}, {demultiplexer_1_out5[31], demultiplexer_1_out5[19:12], demultiplexer_1_out5[20], demultiplexer_1_out5[30:21], 1'b0}};  // Bit_Extender bit_extender_4
  Shifter #(.width(32), .shift("ar")) shifter_1 (.in(bit_extender_3_out), .\dist (5'b00010), .out(shifter_1_out));
  Shifter #(.width(32), .shift("ar")) shifter_2 (.in(bit_extender_4_out), .\dist (5'b00010), .out(shifter_2_out));
  Multiplexer #(.select(3), .width(32), .enable("false")) multiplexer_1 (
    .in1(bit_extender_1_out), .in2(bit_extender_2_out), .in3(shifter_1_out),
    .in4({demultiplexer_1_out4[31:12], {12{1'b0}}}), .in5(shifter_2_out), .out(Output_c6659906), .sel(ImmSel));  // open: in0, in6, in7

  // Other names for the same wires on the sheet: instruction_d05df322[31:0] = instruction; output_sel[2:0] = ImmSel;
  //   result[31:0] = Output_c6659906
endmodule

module branch_Comp (
  input  [31:0] A,
  input  [31:0] B,
  input  BrUn,
  output BrEq,
  output BrLT
);

  wire comparator_1_eq, comparator_1_lt, comparator_2_eq, comparator_2_lt;

  Comparator #(.width(32)) comparator_1 (.a(A), .b(B), .eq(comparator_1_eq), .lt(comparator_1_lt));  // open: gt
  Comparator #(.width(32), .mode("unsigned")) comparator_2 (
    .a(A), .b(B), .eq(comparator_2_eq), .lt(comparator_2_lt));  // open: gt
  Multiplexer #(.enable("false")) multiplexer_1 (.in0(comparator_1_eq), .in1(comparator_2_eq), .out(BrEq), .sel(BrUn));
  Multiplexer #(.enable("false")) multiplexer_2 (.in0(comparator_1_lt), .in1(comparator_2_lt), .out(BrLT), .sel(BrUn));

  // Notes on the sheet:
  //   Input
  //   signed
  //   unsigned
  //   Output
endmodule

module Control_Logic (
  input  BrEq,
  input  BrLT,
  input  [31:0] instruction,
  output PCSel,
  output [2:0] ImmSel,
  output RegWEn,
  output BrUn,
  output BSel,
  output ASel,
  output [3:0] ALUSel,
  output MemRW,
  output [1:0] WBSel,
  output [2:0] load_Sel,
  output [2:0] output_type_Sel
);

  wire addi, and_1_out, and_2_out, andi, comparator_1_eq, comparator_2_eq, comparator_3_eq, comparator_4_eq,
       comparator_5_eq, comparator_6_eq, comparator_7_eq, comparator_8_eq, comparator_9_eq, comparator_10_eq,
       comparator_11_eq, comparator_12_eq, comparator_13_eq, comparator_14_eq, comparator_15_eq,
       comparator_16_eq, comparator_17_eq, comparator_18_eq, comparator_19_eq, comparator_20_eq,
       decoder_1_out0, decoder_1_out1, decoder_1_out4, decoder_1_out6, decoder_2_out0, decoder_2_out1,
       decoder_2_out2, decoder_2_out4, decoder_2_out5, decoder_2_out6, decoder_2_out7, not_1_out, ori,
       SB_type_BrUn, SB_type_PCSel, slli, slti, srai, srli, xori;
  wire [2:0] multiplexer_18_out, multiplexer_20_out, multiplexer_27_out, multiplexer_30_out,
       multiplexer_34_out, multiplexer_38_out, multiplexer_44_out, multiplexer_49_out, multiplexer_50_out,
       multiplexer_51_out, multiplexer_52_out, multiplexer_53_out, multiplexer_55_out, multiplexer_57_out;
  wire [3:0] I_type_ALU_sel, multiplexer_1_out, multiplexer_2_out, multiplexer_4_out, multiplexer_7_out,
       multiplexer_17_out, multiplexer_19_out, multiplexer_21_out, multiplexer_26_out, multiplexer_28_out,
       multiplexer_29_out, multiplexer_31_out, multiplexer_32_out, multiplexer_33_out, multiplexer_35_out,
       multiplexer_37_out, multiplexer_39_out, multiplexer_40_out, multiplexer_46_out, R_type_ALU_sel;
  wire [6:0] multiplexer_8_out, multiplexer_9_out, multiplexer_10_out, multiplexer_11_out,
       multiplexer_12_out, multiplexer_13_out, multiplexer_14_out, multiplexer_22_out, multiplexer_23_out,
       multiplexer_24_out, multiplexer_25_out, multiplexer_36_out;

  Decoder #(.select(3), .enable("false")) decoder_1 (
    .out0(decoder_1_out0), .out1(decoder_1_out1), .out4(decoder_1_out4), .out6(decoder_1_out6),
    .sel(instruction[14:12]));  // open: out2, out3, out5, out7
  Multiplexer #(.width(4), .enable("false")) multiplexer_1 (
    .in0(4'b0000), .in1(4'b0000), .out(multiplexer_1_out), .sel(comparator_9_eq));
  Decoder #(.select(3), .enable("false")) decoder_2 (
    .out0(decoder_2_out0), .out1(decoder_2_out1), .out2(decoder_2_out2), .out4(decoder_2_out4),
    .out5(decoder_2_out5), .out6(decoder_2_out6), .out7(decoder_2_out7), .sel(instruction[14:12]));  // open: out3
  and and_1 (and_1_out, BrEq, decoder_1_out0);
  Comparator #(.width(7), .mode("unsigned")) comparator_1 (
    .a(instruction[6:0]), .b(7'b0110011), .eq(comparator_1_eq));  // open: gt, lt
  Comparator #(.width(7), .mode("unsigned")) comparator_2 (
    .a(instruction[6:0]), .b(7'b0000011), .eq(comparator_2_eq));  // open: gt, lt
  Comparator #(.width(7), .mode("unsigned")) comparator_3 (
    .a(instruction[6:0]), .b(7'b0010011), .eq(comparator_3_eq));  // open: gt, lt
  Comparator #(.width(7), .mode("unsigned")) comparator_4 (
    .a(instruction[6:0]), .b(7'b0100011), .eq(comparator_4_eq));  // open: gt, lt
  Comparator #(.width(7), .mode("unsigned")) comparator_5 (
    .a(instruction[6:0]), .b(7'b1100011), .eq(comparator_5_eq));  // open: gt, lt
  Comparator #(.width(7), .mode("unsigned")) comparator_6 (
    .a(instruction[6:0]), .b(7'b0110111), .eq(comparator_6_eq));  // open: gt, lt
  Comparator #(.width(7), .mode("unsigned")) comparator_7 (
    .a(instruction[6:0]), .b(7'b1101111), .eq(comparator_7_eq));  // open: gt, lt
  Comparator #(.width(7), .mode("unsigned")) comparator_8 (
    .a(instruction[6:0]), .b(7'b1100111), .eq(comparator_8_eq));  // open: gt, lt
  Multiplexer #(.width(4), .enable("false")) multiplexer_2 (
    .in0(multiplexer_1_out), .in1(4'b0001), .out(multiplexer_2_out), .sel(comparator_16_eq));
  not not_1 (not_1_out, BrEq);
  Multiplexer #(.select(3), .enable("false")) multiplexer_3 (
    .in0(1'b0), .in1(1'b0), .in2(1'b0), .in3(1'b0), .in4(SB_type_PCSel), .in5(1'b0), .in6(1'b1), .in7(1'b1),
    .out(PCSel), .sel(output_type_Sel));
  Multiplexer #(.width(4), .enable("false")) multiplexer_4 (
    .in0(multiplexer_2_out), .in1(4'b0010), .out(multiplexer_4_out), .sel(comparator_20_eq));
  and and_2 (and_2_out, not_1_out, decoder_1_out1);
  Multiplexer #(.select(3), .enable("false")) multiplexer_5 (
    .in0(1'b0), .in1(1'b1), .in2(1'b1), .in3(1'b1), .in4(1'b1), .in5(1'b1), .in6(1'b1), .in7(1'b1),
    .out(BSel), .sel(output_type_Sel));
  Multiplexer #(.select(3), .enable("false")) multiplexer_6 (
    .in0(1'b0), .in1(1'b0), .in2(1'b0), .in3(1'b1), .in4(1'b0), .in5(1'b0), .in6(1'b0), .in7(1'b0),
    .out(MemRW), .sel(output_type_Sel));
  Multiplexer #(.width(4), .enable("false")) multiplexer_7 (
    .in0(multiplexer_4_out), .in1(4'b0011), .out(multiplexer_7_out), .sel(comparator_10_eq));
  Multiplexer #(.width(7), .enable("false")) multiplexer_8 (
    .in0(7'b0110011), .in1(instruction[31:25]), .out(multiplexer_8_out), .sel(decoder_2_out0));
  Multiplexer #(.width(7), .enable("false")) multiplexer_9 (
    .in0(7'b0110011), .in1(instruction[31:25]), .out(multiplexer_9_out), .sel(decoder_2_out1));
  Multiplexer #(.width(7), .enable("false")) multiplexer_10 (
    .in0(7'b0110011), .in1(instruction[31:25]), .out(multiplexer_10_out), .sel(decoder_2_out2));
  Multiplexer #(.width(7), .enable("false")) multiplexer_11 (
    .in0(7'b0110011), .in1(instruction[31:25]), .out(multiplexer_11_out), .sel(decoder_2_out4));
  Multiplexer #(.width(7), .enable("false")) multiplexer_12 (
    .in0(7'b0110011), .in1(instruction[31:25]), .out(multiplexer_12_out), .sel(decoder_2_out5));
  Multiplexer #(.width(7), .enable("false")) multiplexer_13 (
    .in0(7'b0110011), .in1(instruction[31:25]), .out(multiplexer_13_out), .sel(decoder_2_out6));
  Multiplexer #(.width(7), .enable("false")) multiplexer_14 (
    .in0(7'b0110011), .in1(instruction[31:25]), .out(multiplexer_14_out), .sel(decoder_2_out7));
  Multiplexer #(.select(3), .enable("false")) multiplexer_15 (
    .in0(and_1_out), .in1(and_2_out), .in4(1'b1), .in6(1'b1), .out(SB_type_PCSel), .sel(instruction[14:12]));  // open: in2, in3, in5, in7
  Multiplexer #(.select(3), .enable("false")) multiplexer_16 (
    .in4(1'b0), .in6(1'b1), .out(SB_type_BrUn), .sel(instruction[14:12]));  // open: in0, in1, in2, in3, in5, in7
  Multiplexer #(.width(4), .enable("false")) multiplexer_17 (
    .in0(multiplexer_7_out), .in1(4'b0100), .out(multiplexer_17_out), .sel(comparator_17_eq));
  Comparator #(.width(7), .mode("unsigned")) comparator_9 (
    .a({7{1'b0}}), .b(multiplexer_8_out), .eq(comparator_9_eq));  // open: gt, lt
  Comparator #(.width(7), .mode("unsigned")) comparator_10 (
    .a({7{1'b0}}), .b(multiplexer_9_out), .eq(comparator_10_eq));  // open: gt, lt
  Comparator #(.width(7), .mode("unsigned")) comparator_11 (
    .a({7{1'b0}}), .b(multiplexer_10_out), .eq(comparator_11_eq));  // open: gt, lt
  Comparator #(.width(7), .mode("unsigned")) comparator_12 (
    .a({7{1'b0}}), .b(multiplexer_11_out), .eq(comparator_12_eq));  // open: gt, lt
  Comparator #(.width(7), .mode("unsigned")) comparator_13 (
    .a({7{1'b0}}), .b(multiplexer_12_out), .eq(comparator_13_eq));  // open: gt, lt
  Comparator #(.width(7), .mode("unsigned")) comparator_14 (
    .a({7{1'b0}}), .b(multiplexer_13_out), .eq(comparator_14_eq));  // open: gt, lt
  Comparator #(.width(7), .mode("unsigned")) comparator_15 (
    .a({7{1'b0}}), .b(multiplexer_14_out), .eq(comparator_15_eq));  // open: gt, lt
  Multiplexer #(.width(3), .enable("false")) multiplexer_18 (
    .in0(3'b000), .in1(3'b000), .out(multiplexer_18_out), .sel(comparator_1_eq));
  Multiplexer #(.width(4), .enable("false")) multiplexer_19 (
    .in0(multiplexer_17_out), .in1(4'b0101), .out(multiplexer_19_out), .sel(comparator_11_eq));
  Decoder #(.select(3), .enable("false")) decoder_3 (
    .out0(addi), .out1(slli), .out2(slti), .out3(xori), .out4(srli), .out5(srai), .out6(ori), .out7(andi),
    .sel(instruction[14:12]));
  Multiplexer #(.width(3), .enable("false")) multiplexer_20 (
    .in0(multiplexer_18_out), .in1(3'b001), .out(multiplexer_20_out), .sel(comparator_8_eq));
  Multiplexer #(.width(4), .enable("false")) multiplexer_21 (
    .in0(multiplexer_19_out), .in1(4'b0110), .out(multiplexer_21_out), .sel(comparator_12_eq));
  Multiplexer #(.width(7), .enable("false")) multiplexer_22 (
    .in0(7'b0110011), .in1(instruction[31:25]), .out(multiplexer_22_out), .sel(decoder_2_out0));
  Multiplexer #(.width(7), .enable("false")) multiplexer_23 (
    .in0(7'b0110011), .in1(instruction[31:25]), .out(multiplexer_23_out), .sel(decoder_2_out1));
  Multiplexer #(.width(7), .enable("false")) multiplexer_24 (
    .in0(7'b0110011), .in1(instruction[31:25]), .out(multiplexer_24_out), .sel(decoder_2_out4));
  Multiplexer #(.width(7), .enable("false")) multiplexer_25 (
    .in0(7'b0110011), .in1(instruction[31:25]), .out(multiplexer_25_out), .sel(decoder_2_out6));
  Multiplexer #(.width(4), .enable("false")) multiplexer_26 (
    .in0(4'b0000), .in1(4'b0000), .out(multiplexer_26_out), .sel(addi));
  Multiplexer #(.width(3), .enable("false")) multiplexer_27 (
    .in0(multiplexer_20_out), .in1(3'b001), .out(multiplexer_27_out), .sel(comparator_2_eq));
  Multiplexer #(.width(4), .enable("false")) multiplexer_28 (
    .in0(multiplexer_21_out), .in1(4'b0111), .out(multiplexer_28_out), .sel(comparator_18_eq));
  Comparator #(.width(7), .mode("unsigned")) comparator_16 (
    .a(7'b0000001), .b(multiplexer_22_out), .eq(comparator_16_eq));  // open: gt, lt
  Comparator #(.width(7), .mode("unsigned")) comparator_17 (
    .a(7'b0000001), .b(multiplexer_23_out), .eq(comparator_17_eq));  // open: gt, lt
  Comparator #(.width(7), .mode("unsigned")) comparator_18 (
    .a(7'b0000001), .b(multiplexer_24_out), .eq(comparator_18_eq));  // open: gt, lt
  Comparator #(.width(7), .mode("unsigned")) comparator_19 (
    .a(7'b0000001), .b(multiplexer_25_out), .eq(comparator_19_eq));  // open: gt, lt
  Multiplexer #(.width(4), .enable("false")) multiplexer_29 (
    .in0(multiplexer_26_out), .in1(4'b0011), .out(multiplexer_29_out), .sel(slli));
  Multiplexer #(.width(3), .enable("false")) multiplexer_30 (
    .in0(multiplexer_27_out), .in1(3'b001), .out(multiplexer_30_out), .sel(comparator_3_eq));
  Multiplexer #(.width(4), .enable("false")) multiplexer_31 (
    .in0(multiplexer_28_out), .in1(4'b1000), .out(multiplexer_31_out), .sel(comparator_13_eq));
  Multiplexer #(.width(4), .enable("false")) multiplexer_32 (
    .in0(multiplexer_29_out), .in1(4'b0101), .out(multiplexer_32_out), .sel(slti));
  Multiplexer #(.width(4), .enable("false")) multiplexer_33 (
    .in0(multiplexer_32_out), .in1(4'b0110), .out(multiplexer_33_out), .sel(xori));
  Multiplexer #(.width(3), .enable("false")) multiplexer_34 (
    .in0(multiplexer_30_out), .in1(3'b010), .out(multiplexer_34_out), .sel(comparator_4_eq));
  Multiplexer #(.width(4), .enable("false")) multiplexer_35 (
    .in0(multiplexer_31_out), .in1(4'b1001), .out(multiplexer_35_out), .sel(comparator_14_eq));
  Multiplexer #(.width(7), .enable("false")) multiplexer_36 (
    .in0(7'b0110011), .in1(instruction[31:25]), .out(multiplexer_36_out), .sel(decoder_2_out0));
  Multiplexer #(.width(4), .enable("false")) multiplexer_37 (
    .in0(multiplexer_33_out), .in1(4'b1000), .out(multiplexer_37_out), .sel(srli));
  Multiplexer #(.width(3), .enable("false")) multiplexer_38 (
    .in0(multiplexer_34_out), .in1(3'b011), .out(multiplexer_38_out), .sel(comparator_5_eq));
  Multiplexer #(.width(4), .enable("false")) multiplexer_39 (
    .in0(multiplexer_35_out), .in1(4'b1010), .out(multiplexer_39_out), .sel(comparator_19_eq));
  Comparator #(.width(7), .mode("unsigned")) comparator_20 (
    .a(7'b0100000), .b(multiplexer_36_out), .eq(comparator_20_eq));  // open: gt, lt
  Multiplexer #(.width(4), .enable("false")) multiplexer_40 (
    .in0(multiplexer_37_out), .in1(4'b1001), .out(multiplexer_40_out), .sel(ori));
  Multiplexer #(.select(3), .enable("false")) multiplexer_41 (
    .in0(1'b1), .in1(1'b1), .in2(1'b1), .in3(1'b0), .in4(1'b0), .in5(1'b1), .in6(1'b1), .in7(1'b1),
    .out(RegWEn), .sel(output_type_Sel));
  Multiplexer #(.select(3), .enable("false")) multiplexer_42 (
    .in0(1'b0), .in1(1'b0), .in2(1'b0), .in3(1'b0), .in4(1'b1), .in5(1'b0), .in6(1'b1), .in7(1'b0),
    .out(ASel), .sel(output_type_Sel));
  Multiplexer #(.select(3), .width(2), .enable("false")) multiplexer_43 (
    .in0(2'b01), .in1(2'b00), .in2(2'b01), .in3(2'b00), .in4(2'b11), .in5(2'b01), .in6(2'b10), .in7(2'b10),
    .out(WBSel), .sel(output_type_Sel));
  Multiplexer #(.width(3), .enable("false")) multiplexer_44 (
    .in0(multiplexer_38_out), .in1(3'b100), .out(multiplexer_44_out), .sel(comparator_6_eq));
  Multiplexer #(.width(4), .enable("false")) multiplexer_45 (
    .in0(multiplexer_39_out), .in1(4'b1011), .out(R_type_ALU_sel), .sel(comparator_15_eq));
  Multiplexer #(.width(4), .enable("false")) multiplexer_46 (
    .in0(multiplexer_40_out), .in1(4'b1011), .out(multiplexer_46_out), .sel(andi));
  Multiplexer #(.width(4), .enable("false")) multiplexer_47 (
    .in0(multiplexer_46_out), .in1(4'b1100), .out(I_type_ALU_sel), .sel(srai));
  Multiplexer #(.width(3), .enable("false")) multiplexer_48 (
    .in0(multiplexer_44_out), .in1(3'b101), .out(ImmSel), .sel(comparator_7_eq));
  Multiplexer #(.width(3), .enable("false")) multiplexer_49 (
    .in0(3'b000), .in1(3'b000), .out(multiplexer_49_out), .sel(comparator_1_eq));
  Multiplexer #(.width(3), .enable("false")) multiplexer_50 (
    .in0(multiplexer_49_out), .in1(3'b001), .out(multiplexer_50_out), .sel(comparator_2_eq));
  Multiplexer #(.width(3), .enable("false")) multiplexer_51 (
    .in0(multiplexer_50_out), .in1(3'b010), .out(multiplexer_51_out), .sel(comparator_3_eq));
  Multiplexer #(.width(3), .enable("false")) multiplexer_52 (
    .in0(multiplexer_51_out), .in1(3'b011), .out(multiplexer_52_out), .sel(comparator_4_eq));
  Multiplexer #(.width(3), .enable("false")) multiplexer_53 (
    .in0(multiplexer_52_out), .in1(3'b100), .out(multiplexer_53_out), .sel(comparator_5_eq));
  Multiplexer #(.select(3), .enable("false")) multiplexer_54 (
    .in4(SB_type_BrUn), .out(BrUn), .sel(output_type_Sel));  // open: in0, in1, in2, in3, in5, in6, in7
  Multiplexer #(.width(3), .enable("false")) multiplexer_55 (
    .in0(multiplexer_53_out), .in1(3'b101), .out(multiplexer_55_out), .sel(comparator_6_eq));
  Multiplexer #(.select(3), .width(4), .enable("false")) multiplexer_56 (
    .in0(R_type_ALU_sel), .in1(4'b0000), .in2(I_type_ALU_sel), .in3(4'b0000), .in4(4'b0000), .in5(4'b0000),
    .in6(4'b0000), .in7(4'b0000), .out(ALUSel), .sel(output_type_Sel));
  Multiplexer #(.width(3), .enable("false")) multiplexer_57 (
    .in0(multiplexer_55_out), .in1(3'b110), .out(multiplexer_57_out), .sel(comparator_7_eq));
  Multiplexer #(.width(3), .enable("false")) multiplexer_58 (
    .in0(multiplexer_57_out), .in1(3'b111), .out(output_type_Sel), .sel(comparator_8_eq));

  assign load_Sel = instruction[14:12];

  // Other names for the same wires on the sheet: ALUSel_ba110e7f[3:0] = ALUSel; ASel_033552a1 = ASel;
  //   BrUn_4e1d2fd5 = BrUn; BSel_3c3d71b8 = BSel; instruction_d05df322[31:0] = instruction;
  //   opcode_e39ec391[6:0] = instruction[6:0]; funct3_d2934c05[2:0] = instruction[14:12];
  //   funct7_c4b0fdb4[6:0] = instruction[31:25]; MemRW_8a670354 = MemRW; PCSel_09d1e959 = PCSel;
  //   RegWEn_136dac0f = RegWEn; type_sel[2:0] = ImmSel; WBSel_7e3281e0[1:0] = WBSel

  // Notes on the sheet:
  //   Input
  //   beq
  //   blt
  //   R_type_setup
  //   SB_type_setup
  //   bne
  //   bltu
  //   Find type
  //   I_type_with_load_setup
  //   I_type_setup
  //   Output
  //   U_type_setup
  //   0:+4_1:alu
  //   0:reg_1:imm
  //   0:reg_1:pc
  //   0:read_1:write
  //   0:dataR_1::alu_2:+4
  //   UJ_type_setup
  //   S_type_setup
  //   jalr_type_setup
endmodule

module load_control (
  input  [31:0] MEMData,
  input  [2:0] load_Sel,
  output [31:0] output_05da9558
);

  wire [7:0] bitselector_1_out;
  wire [15:0] bitselector_2_out;
  wire [31:0] bit_extender_1_out, bit_extender_2_out;

  BitSelector #(.width(32), .group(8)) bitselector_1 (.in(MEMData), .out(bitselector_1_out));  // open: sel
  BitSelector #(.width(32), .group(16)) bitselector_2 (.in(MEMData), .out(bitselector_2_out));  // open: sel
  assign bit_extender_1_out = {{24{bitselector_1_out[7]}}, bitselector_1_out};  // Bit_Extender bit_extender_1
  assign bit_extender_2_out = {{16{bitselector_2_out[15]}}, bitselector_2_out};  // Bit_Extender bit_extender_2
  Multiplexer #(.select(3), .width(32), .enable("false")) multiplexer_1 (
    .in0(bit_extender_1_out), .in1(bit_extender_2_out), .in2(MEMData), .out(output_05da9558), .sel(load_Sel));  // open: in3, in4, in5, in6, in7
endmodule

module jalr_type_Rshift (
  input  [31:0] intput_6fd505b9,
  input  [2:0] immSel_50e67bb1,
  output [31:0] output_a7d0038a
);

  wire [31:0] demultiplexer_1_out0, demultiplexer_1_out1, demultiplexer_1_out2, demultiplexer_1_out3,
       demultiplexer_1_out4, demultiplexer_1_out5, demultiplexer_1_out6, demultiplexer_1_out7, shifter_1_out;

  Demultiplexer #(.select(3), .width(32), .enable("false")) demultiplexer_1 (
    .out0(demultiplexer_1_out0), .out1(demultiplexer_1_out1), .out2(demultiplexer_1_out2),
    .out3(demultiplexer_1_out3), .out4(demultiplexer_1_out4), .out5(demultiplexer_1_out5),
    .out6(demultiplexer_1_out6), .out7(demultiplexer_1_out7), .in(intput_6fd505b9), .sel(immSel_50e67bb1));
  Shifter #(.width(32), .shift("ar")) shifter_1 (.in(demultiplexer_1_out7), .\dist (5'b00010), .out(shifter_1_out));
  Multiplexer #(.select(3), .width(32), .enable("false")) multiplexer_1 (
    .in0(demultiplexer_1_out0), .in1(demultiplexer_1_out1), .in2(demultiplexer_1_out2),
    .in3(demultiplexer_1_out3), .in4(demultiplexer_1_out4), .in5(demultiplexer_1_out5),
    .in6(demultiplexer_1_out6), .in7(shifter_1_out), .out(output_a7d0038a), .sel(immSel_50e67bb1));
endmodule

module jalr_type_Lshift (
  input  [31:0] input_0c2948f0,
  input  [2:0] type_sel,
  output [31:0] output_99ad1175
);

  wire [31:0] demultiplexer_1_out0, demultiplexer_1_out1, demultiplexer_1_out2, demultiplexer_1_out3,
       demultiplexer_1_out4, demultiplexer_1_out5, demultiplexer_1_out6, demultiplexer_1_out7, shifter_1_out;

  Demultiplexer #(.select(3), .width(32), .enable("false")) demultiplexer_1 (
    .out0(demultiplexer_1_out0), .out1(demultiplexer_1_out1), .out2(demultiplexer_1_out2),
    .out3(demultiplexer_1_out3), .out4(demultiplexer_1_out4), .out5(demultiplexer_1_out5),
    .out6(demultiplexer_1_out6), .out7(demultiplexer_1_out7), .in(input_0c2948f0), .sel(type_sel));
  Shifter #(.width(32)) shifter_1 (.in(demultiplexer_1_out7), .\dist (5'b00010), .out(shifter_1_out));
  Multiplexer #(.select(3), .width(32), .enable("false")) multiplexer_1 (
    .in0(demultiplexer_1_out0), .in1(demultiplexer_1_out1), .in2(demultiplexer_1_out2),
    .in3(demultiplexer_1_out3), .in4(demultiplexer_1_out4), .in5(demultiplexer_1_out5),
    .in6(demultiplexer_1_out6), .in7(shifter_1_out), .out(output_99ad1175), .sel(type_sel));
endmodule

module IF_EX_control (
  input  [31:0] PC_PLUS_4,
  input  [31:0] ALU_6e8fb84a,
  input  [31:0] PC_6faf80e7,
  input  [31:0] instruction,
  input  clock,
  input  branch_eq,
  input  branch_lt,
  output [31:0] PC_PULS_4_OUT,
  output [31:0] ALU_OUT_6acabea4,
  output [31:0] PC_OUT_758b2ec9,
  output [31:0] instruction_OUT_f61fd319
);

  wire after_first, and_5_out, and_6_out, and_7_out, and_8_out, beq, blt, bltu, bne, comparator_9_eq,
       comparator_10_eq, comparator_11_eq, comparator_12_eq, jal, jalr, Kill, not_1_out, SB_type;
  wire [31:0] multiplexer_1_out, register_2_q;

  Comparator #(.width(7), .mode("unsigned")) comparator_1 (.a(instruction[6:0]), .b(7'b0110011));  // open: gt, eq, lt
  Comparator #(.width(7), .mode("unsigned")) comparator_2 (.a(instruction[6:0]), .b(7'b0000011));  // open: gt, eq, lt
  Comparator #(.width(7), .mode("unsigned")) comparator_3 (.a(instruction[6:0]), .b(7'b0010011));  // open: gt, eq, lt
  Comparator #(.width(7), .mode("unsigned")) comparator_4 (.a(instruction[6:0]), .b(7'b0100011));  // open: gt, eq, lt
  Comparator #(.width(7), .mode("unsigned")) comparator_5 (
    .a(instruction[6:0]), .b(7'b1100011), .eq(SB_type));  // open: gt, lt
  Comparator #(.width(7), .mode("unsigned")) comparator_6 (.a(instruction[6:0]), .b(7'b0110111));  // open: gt, eq, lt
  Comparator #(.width(7), .mode("unsigned")) comparator_7 (
    .a(instruction[6:0]), .b(7'b1101111), .eq(jal));  // open: gt, lt
  Comparator #(.width(7), .mode("unsigned")) comparator_8 (
    .a(instruction[6:0]), .b(7'b1100111), .eq(jalr));  // open: gt, lt
  Comparator #(.width(3), .mode("unsigned")) comparator_9 (
    .a(instruction[14:12]), .b(3'b000), .eq(comparator_9_eq));  // open: gt, lt
  Comparator #(.width(3), .mode("unsigned")) comparator_10 (
    .a(instruction[14:12]), .b(3'b001), .eq(comparator_10_eq));  // open: gt, lt
  Comparator #(.width(3), .mode("unsigned")) comparator_11 (
    .a(instruction[14:12]), .b(3'b100), .eq(comparator_11_eq));  // open: gt, lt
  Comparator #(.width(3), .mode("unsigned")) comparator_12 (
    .a(instruction[14:12]), .b(3'b110), .eq(comparator_12_eq));  // open: gt, lt
  and and_1 (beq, comparator_9_eq, SB_type);
  and and_2 (bne, comparator_10_eq, SB_type);
  and and_3 (blt, comparator_11_eq, SB_type);
  and and_4 (bltu, comparator_12_eq, SB_type);
  Multiplexer #(.width(32), .enable("false")) multiplexer_1 (
    .in0(instruction), .in1({32{1'b0}}), .out(multiplexer_1_out), .sel(after_first));
  Register #(.width(1)) register_1 (.D(Kill), .clk(clock), .Q(after_first));  // open: en, clr
  Register #(.width(32)) register_2 (.D(multiplexer_1_out), .clk(clock), .Q(register_2_q));  // open: en, clr
  not not_1 (not_1_out, branch_eq);
  and and_5 (and_5_out, beq, branch_eq);
  and and_6 (and_6_out, bne, not_1_out);
  and and_7 (and_7_out, blt, branch_lt);
  and and_8 (and_8_out, bltu, branch_lt);
  Multiplexer #(.width(32), .enable("false")) multiplexer_2 (
    .in0(multiplexer_1_out), .in1(register_2_q), .out(instruction_OUT_f61fd319), .sel(after_first));
  or or_1 (Kill, jalr, jal, and_5_out, and_6_out, and_7_out, and_8_out);

  assign ALU_OUT_6acabea4 = ALU_6e8fb84a;
  assign PC_OUT_758b2ec9 = PC_6faf80e7;
  assign PC_PULS_4_OUT = PC_PLUS_4;

  // Other names for the same wires on the sheet: branch_eq_e99249f2 = branch_eq; branch_lt_b8f0432b = branch_lt;
  //   clk = clock; instruction_7c7060d8[31:0] = instruction; opcode_f9384849[6:0] = instruction[6:0];
  //   funct_9bbad175[2:0] = instruction[14:12]
endmodule
